# Fritzing sketch dwr-controller-v0.1 (saved by Fritzing 0.9.3b)
breadboards: 1

parts:
  S1 = Pushbutton [package="[THT]"]
  S2 = Pushbutton [package="[THT]"]
  IC3 = IC, DIP package, 14 pins [chip_label=CD4066B]
  R1 = Resistor [tolerance=±0.5% resistance=6.8 package=THT]
  R2 = Resistor [tolerance=±0.5% resistance=6.8 package=THT]
  R3 = Resistor [tolerance=±0.5% resistance=6.8 package=THT]
  R4 = Resistor [tolerance=±0.5% resistance=6.8 package=THT]
  Part3 = Arduino Nano (Rev3.0)
  Grove1 = Grove OLED 128x96
  Part4 = KY-003 Hall Magnetic Sensor Module [package="Breakout board"]
  S3 = Round Pushbutton
  S4 = Round Pushbutton
  S5 = Round Pushbutton
  S6 = Round Pushbutton

nets:
  GND: S1.Pin_1, S1.Pin_2, S2.Pin_1, S2.Pin_2, IC3.pin7, R1.Pin_1, R2.Pin_1, R3.Pin_1, R4.Pin_1, Part3.GND, Grove1.GND, Part4.-
  N1: S1.Pin_3, S1.Pin_4, Part3.D4
  N2: S2.Pin_3, S2.Pin_4, Part3.D5
  N3: IC3.pin1, S6.leg1
  N4: IC3.pin2, S6.leg0
  N5: IC3.pin3, S5.leg1
  N6: IC3.pin4, S5.leg0
  N7: IC3.pin5, R1.Pin_0, Part3.D7
  N8: IC3.pin6, R2.Pin_0, Part3.D8
  N9: IC3.pin8, S4.leg1
  N10: IC3.pin9, S4.leg0
  N11: IC3.pin10, S3.leg1
  N12: IC3.pin11, S3.leg0
  N13: IC3.pin12, R4.Pin_0, Part3.D9
  N14: IC3.pin13, R3.Pin_0, Part3.D6
  5V: IC3.pin14, Part3.5V, Grove1.VCC, Part4.Vin
  N15: Part3.D3, Part4.S
  N16: Part3.A5, Grove1.SCL
  N17: Part3.A4, Grove1.SDA

custom parts:
  KY-003 Hall Magnetic Sensor Module: KEYES KY-003 Arduino Hall Magnetic Sensor Module is a switch that will turn on/off in the presence of a magnetic field.
